# Fritzing sketch ArduinoLayout (saved by Fritzing 0.9.3b)
breadboards: 1

parts:
  Part1 = Arduino Uno (Rev3)
  S1 = Momentary Switch [package=ksa_sealed_tac_switch]
  R1 = Resistor [tolerance=±5% resistance=220 package=THT]

nets:
  N1: Part1.D2, S1.1
  N2: Part1.5V, S1.4
  N3: Part1.GND, R1.Pin_1
  N4: S1.2, R1.Pin_0
